// Digital circuit MUX schematic.dig as structural Verilog
module MUX_schematic (
  input  A,
  input  B,
  input  C,
  input  D,
  output Y
);

  wire _7404_1_pin5, _7404_1_pin9, _7404_1_pin11, _7404_1_pin13, _74151_1_pin14, _74151_1_pin15;

  _74151 _74151_1 (
    .pin1(D), .pin2(D), .pin3(D), .pin4(1'b1), .pin5(Y), .pin7(1'b0), .pin8(1'b0), .pin9(C), .pin10(B),
    .pin11(A), .pin12(1'b0), .pin13(1'b1), .pin14(_74151_1_pin14), .pin15(_74151_1_pin15), .pin16(1'b1));  // open: pin6
  _7404 _7404_1 (
    .pin1(D), .pin2(_74151_1_pin15), .pin3(D), .pin4(_74151_1_pin14), .pin5(_7404_1_pin5), .pin7(1'b0),
    .pin9(_7404_1_pin9), .pin11(_7404_1_pin11), .pin13(_7404_1_pin13), .pin14(1'b1));  // open: pin6, pin8, pin10, pin12
  // NotConnected on _7404_1_pin5
  // NotConnected on _7404_1_pin13
  // NotConnected on _7404_1_pin11
  // NotConnected on _7404_1_pin9
endmodule
